# Fritzing sketch ledbridge 구성회로도 (saved by Fritzing 0.9.4)
circuit board: 8.46667cm x 5.64444cm
breadboards: 1

parts:
  U1 = WS2812 RGB LED strip
  부품1 = Arduino Nano (Rev3.0)
  rst_버튼 = Round Pushbutton
  LCD1 = LCD screen
  power_버튼_(long) = Round Pushbutton
  ok_버튼 = Round Pushbutton
  R1 = Resistor [tolerance=±5% resistance=10 package=THT]
  R2 = Resistor [tolerance=±5% resistance=10 package=THT]
  R3 = Rotary Potentiometer (Small) [maximum_resistance=100kΩ package=THT]
  VCC1 = 4 x AAA Battery Mount
  사운드_센서 = Breakout Board for Electret Microphone
  LCM1602_IIC1 = LCM1602 IIC [part_number="LCM1602 IIC" chip_label="LCM1602 IIC" package="DIP (Dual Inline) [THT]"]

nets:
  GND: U1.GND, 부품1.GND, rst_버튼.leg0, R3.leg1, VCC1.-, 사운드_센서.GND, LCM1602_IIC1.GND
  N1: U1.VCC, VCC1.+
  N2: U1.DOUT, 부품1.D6
  N3: 부품1.D0/RX, 부품1.RESET, rst_버튼.leg1
  N4: 부품1.D2, 부품1.D3, R1.Pin_0, R2.Pin_0
  VCC: 부품1.5V, power_버튼_(long).leg1, ok_버튼.leg1, R3.leg2, 사운드_센서.VCC, LCM1602_IIC1.VCC
  N5: 부품1.A5, LCM1602_IIC1.SCL
  N6: 부품1.A4, LCM1602_IIC1.SDA
  N7: 부품1.A2, 사운드_센서.AUD
  N8: 부품1.A0, R3.wiper
  N9: LCD1.VSS, LCM1602_IIC1.K
  N10: LCD1.VDD, LCM1602_IIC1.A
  N11: LCD1.V0, LCM1602_IIC1.D7
  N12: LCD1.RS, LCM1602_IIC1.D5
  N13: LCD1.R/W, LCM1602_IIC1.D3
  N14: LCD1.E, LCM1602_IIC1.D6
  N15: LCD1.DB0, LCM1602_IIC1.D4
  N16: LCD1.DB1, LCM1602_IIC1.D2
  N17: LCD1.DB2, LCM1602_IIC1.D1
  N18: LCD1.DB3, LCM1602_IIC1.D0
  N19: LCD1.DB4, LCM1602_IIC1.E
  N20: LCD1.DB5, LCM1602_IIC1.RW
  N21: LCD1.DB6, LCM1602_IIC1.RS
  N22: LCD1.DB7, LCM1602_IIC1.V0
  N23: LCD1.LED+, LCM1602_IIC1.VDD
  N24: LCD1.LED-, LCM1602_IIC1.VSS
  N25: power_버튼_(long).leg0, R1.Pin_1
  N26: ok_버튼.leg0, R2.Pin_1

custom parts:
  WS2812 RGB LED strip: WS2812 strip
  LCM1602 IIC: I2C-Module to use a 1602 or 2004 LCD on with the wire.h libory Serial LCD Modul
